// Logisim project 5-stage-cpu-ideal.circ as structural Verilog: 8 circuits, main circuit main
module main (
  input  Rst
);

  wire alu_1_equal, branch_1_pcsrc, Clk, ComClk, control_1_aluysrc2, control_1_disp, control_1_dmwe,
       control_1_halt, control_1_pcaddsrc, control_1_rfr1src, control_1_rfwe, ex_mem_1_dispdout,
       ex_mem_1_dmwedout, ex_mem_1_haltdout, ex_mem_1_rfwedout, Halt, id_ex_1_aluysrc2dout, id_ex_1_dispdout,
       id_ex_1_dmwedout, id_ex_1_haltdout, id_ex_1_pcaddsrcdout, id_ex_1_rfwedout, mem_wb_1_rfwedout,
       not_1_out;
  wire [1:0] branch_1_brpcsrc, control_1_aluysrc, control_1_rfdinsrc, control_1_rfrwsrc,
       ex_mem_1_rfdinsrcdout, id_ex_1_aluysrcdout, id_ex_1_rfdinsrcdout, mem_wb_1_rfdinsrcdout;
  wire [3:0] control_1_aluop, id_ex_1_aluopdout;
  wire [4:0] ex_mem_1_wregdout, id_ex_1_wregdout, insanalyse_1_rd, insanalyse_1_rs, insanalyse_1_rt,
       insanalyse_1_shamt, mem_wb_1_wregdout, multiplexer_4_out, multiplexer_5_out, multiplexer_6_out;
  wire [5:0] control_1_brins, id_ex_1_brinsdout, insanalyse_1_funct, insanalyse_1_op;
  wire [15:0] insanalyse_1_immediate16;
  wire [25:0] insanalyse_1_immediate26;
  wire [31:0] adder_1_out, adder_2_out, adder_3_out, alu_1_result, bit_extender_1_out, bit_extender_2_out,
       bit_extender_3_out, bit_extender_4_out, bit_extender_5_out, counter_1_q, ex_mem_1_aludout,
       ex_mem_1_irdout, ex_mem_1_pcadddout, ex_mem_1_pcdout, ex_mem_1_rfr2dout, id_ex_1_ext5to32dout,
       id_ex_1_ext16to32dout, id_ex_1_irdout, id_ex_1_pc_1dout, id_ex_1_pcdout, id_ex_1_rfr1dout,
       id_ex_1_rfr2dout, id_ex_1_sext16to32dout, id_ex_1_sext26to32dout, if_id_1_irdout, if_id_1_pc_1dout,
       if_id_1_pcdout, main_1_reg1, main_1_reg2_2, main_1_v0_value, mem_wb_1_aludout, mem_wb_1_dmdout,
       mem_wb_1_pcadddout, mem_wb_1_sext16to32dout, multiplexer_1_out, multiplexer_2_out, multiplexer_3_out,
       multiplexer_7_out, multiplexer_8_out, multiplexer_9_out, multiplexer_10_out, PC_q, ram_1_data,
       rom_1_data;

  Multiplexer #(.width(32), .enable("false")) multiplexer_1 (
    .in0(adder_1_out), .in1(multiplexer_2_out), .out(multiplexer_1_out), .sel(branch_1_pcsrc));
  Multiplexer #(.select(2), .width(32), .enable("false")) multiplexer_2 (
    .in0(id_ex_1_rfr1dout), .in1(id_ex_1_pc_1dout), .in2(adder_3_out), .in3(id_ex_1_sext26to32dout),
    .out(multiplexer_2_out), .sel(branch_1_brpcsrc));
  Register #(.width(32)) PC (.D(multiplexer_1_out), .en(1'b1), .Q(PC_q), .clk(Clk));  // open: clr
  Adder #(.width(32)) adder_1 (.a(32'h1), .b(PC_q), .out(adder_1_out));  // open: cin, cout
  Clock clock_1 (.out(ComClk));
  ROM #(.addrWidth(10), .dataWidth(32)) rom_1 (.addr(PC_q[9:0]), .data(rom_1_data), .sel(1'b1));
  IF_ID if_id_1 (
    .PCDin(PC_q), .IRDin(rom_1_data), .PCDout(if_id_1_pcdout), .IRDout(if_id_1_irdout), .WE(1'b1), .Clk(Clk),
    .Rst(Rst), .PC_1Din(adder_1_out), .PC_1Dout(if_id_1_pc_1dout));
  Counter #(.width(32), .max('hffffffff)) counter_1 (.Q(counter_1_q), .clk(Clk));  // open: load, D, count, carry, clr
  InsAnalyse insanalyse_1 (
    .Ins(if_id_1_irdout), .OP(insanalyse_1_op), .Rs(insanalyse_1_rs), .Rt(insanalyse_1_rt),
    .Rd(insanalyse_1_rd), .Shamt(insanalyse_1_shamt), .funct(insanalyse_1_funct),
    .Immediate16(insanalyse_1_immediate16), .Immediate26(insanalyse_1_immediate26));
  Multiplexer #(.width(32), .enable("false")) multiplexer_3 (
    .in0({32{1'b0}}), .in1(32'h1), .out(multiplexer_3_out), .sel(Halt));
  not not_1 (not_1_out, control_1_rfr1src);
  Adder #(.width(32)) adder_2 (.a(multiplexer_3_out), .b(counter_1_q), .out(adder_2_out));  // open: cin, cout
  // Probe on adder_2_out
  Control control_1 (
    .v0(main_1_v0_value), .OP(insanalyse_1_op), .funct(insanalyse_1_funct), .PCAddSrc(control_1_pcaddsrc),
    .RFR1Src(control_1_rfr1src), .RFRWSrc(control_1_rfrwsrc), .RFDinSrc(control_1_rfdinsrc),
    .RFWE(control_1_rfwe), .ALUYSrc(control_1_aluysrc), .ALUOP(control_1_aluop), .DMWE(control_1_dmwe),
    .Halt(control_1_halt), .Disp(control_1_disp), .ALUYSrc2(control_1_aluysrc2), .BrIns(control_1_brins));  // open: PCEn
  Multiplexer #(.width(5), .enable("false")) multiplexer_4 (
    .in0(insanalyse_1_rs), .in1(insanalyse_1_rt), .out(multiplexer_4_out), .sel(control_1_rfr1src));
  Multiplexer #(.width(5), .enable("false")) multiplexer_5 (
    .in0(insanalyse_1_rs), .in1(insanalyse_1_rt), .out(multiplexer_5_out), .sel(not_1_out));
  Multiplexer #(.select(2), .width(5), .enable("false")) multiplexer_6 (
    .in0(insanalyse_1_rt), .in1(insanalyse_1_rd), .in2({5{1'b1}}), .out(multiplexer_6_out),
    .sel(control_1_rfrwsrc));  // open: in3
  Multiplexer #(.select(2), .width(32), .enable("false")) multiplexer_7 (
    .in0(mem_wb_1_pcadddout), .in1(mem_wb_1_dmdout), .in2(mem_wb_1_aludout), .in3(mem_wb_1_sext16to32dout),
    .out(multiplexer_7_out), .sel(mem_wb_1_rfdinsrcdout));
  regfile_cpu_main main_1 (
    .Reg1_num(multiplexer_4_out), .Reg2(multiplexer_5_out), .Write_Reg_num(mem_wb_1_wregdout),
    .Din(multiplexer_7_out), .Write_Enable(mem_wb_1_rfwedout), .Clock(Clk), .Reg1(main_1_reg1),
    .Reg2_2(main_1_reg2_2), .v0_Value(main_1_v0_value));  // open: s0_Value, s1_Value, s2_Value, ra_Value, a0_Value
  assign bit_extender_1_out = {{27{1'b0}}, insanalyse_1_shamt};  // Bit_Extender bit_extender_1
  assign bit_extender_2_out = {{16{insanalyse_1_immediate16[15]}}, insanalyse_1_immediate16};  // Bit_Extender bit_extender_2
  assign bit_extender_3_out = {{16{1'b0}}, insanalyse_1_immediate16};  // Bit_Extender bit_extender_3
  assign bit_extender_4_out = {{6{insanalyse_1_immediate26[25]}}, insanalyse_1_immediate26};  // Bit_Extender bit_extender_4
  ID_EX id_ex_1 (
    .PCDin(if_id_1_pcdout), .IRDin(if_id_1_irdout), .ALUOPDin(control_1_aluop), .PCDout(id_ex_1_pcdout),
    .IRDout(id_ex_1_irdout), .ALUOPDout(id_ex_1_aluopdout), .WE(1'b1), .Clk(Clk), .Rst(Rst),
    .ALUYSrcDin(control_1_aluysrc), .ALUYSrcDout(id_ex_1_aluysrcdout), .ALUYSrc2Din(control_1_aluysrc2),
    .ALUYSrc2Dout(id_ex_1_aluysrc2dout), .Ext5to32Din(bit_extender_1_out),
    .Ext5to32Dout(id_ex_1_ext5to32dout), .SExt16to32Din(bit_extender_2_out),
    .SExt16to32Dout(id_ex_1_sext16to32dout), .Ext16to32Din(bit_extender_3_out),
    .Ext16to32Dout(id_ex_1_ext16to32dout), .RFR1Din(main_1_reg1), .RFR1Dout(id_ex_1_rfr1dout),
    .RFR2Din(main_1_reg2_2), .RFR2Dout(id_ex_1_rfr2dout), .PC_1Din(if_id_1_pc_1dout),
    .PC_1Dout(id_ex_1_pc_1dout), .DMWEDin(control_1_dmwe), .DMWEDout(id_ex_1_dmwedout),
    .PCAddSrcDin(control_1_pcaddsrc), .PCAddSrcDout(id_ex_1_pcaddsrcdout), .RFWEDin(control_1_rfwe),
    .RFWEDout(id_ex_1_rfwedout), .RFDinSrcDin(control_1_rfdinsrc), .RFDinSrcDout(id_ex_1_rfdinsrcdout),
    .SExt26to32Din(bit_extender_4_out), .SExt26to32Dout(id_ex_1_sext26to32dout), .BrInsDin(control_1_brins),
    .BrInsDout(id_ex_1_brinsdout), .WRegDin(multiplexer_6_out), .WRegDout(id_ex_1_wregdout),
    .DispDin(control_1_disp), .DispDout(id_ex_1_dispdout), .HaltDin(control_1_halt),
    .HaltDout(id_ex_1_haltdout));
  Multiplexer #(.select(2), .width(32), .enable("false")) multiplexer_8 (
    .in0(id_ex_1_rfr2dout), .in1(id_ex_1_ext5to32dout), .in2(id_ex_1_sext16to32dout),
    .in3(id_ex_1_ext16to32dout), .out(multiplexer_8_out), .sel(id_ex_1_aluysrcdout));
  Multiplexer #(.width(32), .disabled(0), .enable("false")) multiplexer_9 (
    .in0(multiplexer_8_out), .in1({32{1'b0}}), .out(multiplexer_9_out), .sel(id_ex_1_aluysrc2dout));
  Multiplexer #(.width(32), .enable("false")) multiplexer_10 (
    .in0({32{1'b0}}), .in1(id_ex_1_sext16to32dout), .out(multiplexer_10_out), .sel(id_ex_1_pcaddsrcdout));
  Branch branch_1 (
    .Equal(alu_1_equal), .Judge(alu_1_result[0]), .BrIns(id_ex_1_brinsdout), .BrPCSrc(branch_1_brpcsrc),
    .PCSrc(branch_1_pcsrc));
  ALU alu_1 (
    .AluOP(id_ex_1_aluopdout), .X(id_ex_1_rfr1dout), .Equal(alu_1_equal), .Result(alu_1_result),
    .Y(multiplexer_9_out));  // open: Signed_Overflow, Result_2, UnSigned_Overflow
  Adder #(.width(32)) adder_3 (
    .a(multiplexer_10_out), .b(id_ex_1_pc_1dout), .out(adder_3_out), .cin(1'b0));  // open: cout
  EX_MEM ex_mem_1 (
    .PCDin(id_ex_1_pcdout), .IRDin(id_ex_1_irdout), .DMWEDin(id_ex_1_dmwedout), .RFWEDin(id_ex_1_rfwedout),
    .RFDinSrcDin(id_ex_1_rfdinsrcdout), .PCDout(ex_mem_1_pcdout), .IRDout(ex_mem_1_irdout),
    .DMWEDout(ex_mem_1_dmwedout), .RFWEDout(ex_mem_1_rfwedout), .RFDinSrcDout(ex_mem_1_rfdinsrcdout),
    .WE(1'b1), .Clk(Clk), .Rst(Rst), .ALUDin(alu_1_result), .ALUDout(ex_mem_1_aludout),
    .RFR2Din(id_ex_1_rfr2dout), .RFR2Dout(ex_mem_1_rfr2dout), .PCAddDin(adder_3_out),
    .PCAddDout(ex_mem_1_pcadddout), .WRegDin(id_ex_1_wregdout), .WRegDout(ex_mem_1_wregdout),
    .HaltDin(id_ex_1_haltdout), .HaltDout(ex_mem_1_haltdout), .DispDin(id_ex_1_dispdout),
    .DispDout(ex_mem_1_dispdout));
  RAM #(.addrWidth(10), .dataWidth(32), .bus("separate")) ram_1 (
    .addr(ex_mem_1_aludout[9:0]), .din(ex_mem_1_rfr2dout), .data(ram_1_data), .str(ex_mem_1_dmwedout),
    .sel(1'b1), .clk(Clk), .ld(1'b1), .clr(1'b0));
  assign bit_extender_5_out = {{16{ram_1_data[15]}}, ram_1_data[15:0]};  // Bit_Extender bit_extender_5
  MEM_WB mem_wb_1 (
    .PCDin(ex_mem_1_pcdout), .IRDin(ex_mem_1_irdout), .RFWEDin(ex_mem_1_rfwedout),
    .RFDinSrcDin(ex_mem_1_rfdinsrcdout), .RFWEDout(mem_wb_1_rfwedout), .RFDinSrcDout(mem_wb_1_rfdinsrcdout),
    .WE(1'b1), .Clk(Clk), .Rst(Rst), .ALUDin(ex_mem_1_aludout), .ALUDout(mem_wb_1_aludout),
    .DMDin(ram_1_data), .DMDout(mem_wb_1_dmdout), .PCAddDin(ex_mem_1_pcadddout),
    .PCAddDout(mem_wb_1_pcadddout), .SExt16to32Din(bit_extender_5_out),
    .SExt16to32Dout(mem_wb_1_sext16to32dout), .WRegDin(ex_mem_1_wregdout), .WRegDout(mem_wb_1_wregdout),
    .HaltDin(ex_mem_1_haltdout), .HaltDout(Halt), .DispDin(ex_mem_1_dispdout));  // open: PCDout, IRDout, DispDout
  and and_1 (Clk, ~Halt, ComClk);  // AND_Gate

  // Notes on the sheet:
  //   contents of rom_1 (hex, n*v repeats v):
  //   20100000 20110000 20120000 20130000 36100000 36310001 36520002 36730003 ae100000 ae110004 ae120008
  //   ae13000c 2002000a 20110000 20120000 20130000 c
endmodule

module InsAnalyse (
  input  [31:0] Ins,
  output [5:0] OP,
  output [4:0] Rs,
  output [4:0] Rt,
  output [4:0] Rd,
  output [4:0] Shamt,
  output [5:0] funct,
  output [15:0] Immediate16,
  output [25:0] Immediate26
);


  assign funct = Ins[5:0];
  assign Immediate16 = Ins[15:0];
  assign Immediate26 = Ins[25:0];
  assign OP = Ins[31:26];
  assign Rd = Ins[15:11];
  assign Rs = Ins[25:21];
  assign Rt = Ins[20:16];
  assign Shamt = Ins[10:6];
endmodule

module Control (
  input  [31:0] v0,
  input  [5:0] OP,
  input  [5:0] funct,
  output [5:0] BrIns,
  output PCAddSrc,
  output PCEn,
  output RFR1Src,
  output [1:0] RFRWSrc,
  output [1:0] RFDinSrc,
  output RFWE,
  output [1:0] ALUYSrc,
  output ALUYSrc2,
  output [3:0] ALUOP,
  output DMWE,
  output Halt,
  output Disp
);

  wire add, addi, addiu, addu, \and , andi, decoder_1_out0, decoder_2_out0, decoder_2_out1, decoder_4_out0,
       decoder_4_out1, lh, lw, \nor , \or , ori, sll, sllv, slt, slti, sltu, sra, srl, srlv, sub, syscall,
       v0_10;
  wire [7:0] or_7_out;
  wire [31:0] subtractor_1_out;

  Decoder #(.select(5), .disabled(0)) decoder_1 (
    .out0(decoder_1_out0), .out1(ALUYSrc2), .out2(BrIns[2]), .out3(BrIns[1]), .out4(BrIns[5]),
    .out5(BrIns[4]), .out8(addi), .out9(addiu), .out10(slti), .out12(andi), .out13(ori), .sel(OP[4:0]),
    .en(decoder_2_out0));  // open: out6, out7, out11, out14, out15, out16, out17, out18, out19, out20, out21, out22, out23, out24, out25, out26, out27, out28, out29, out30, out31
  Decoder #(.enable("false")) decoder_2 (.out0(decoder_2_out0), .out1(decoder_2_out1), .sel(OP[5]));
  Decoder #(.select(5), .disabled(0)) decoder_3 (
    .out1(lh), .out3(lw), .out11(DMWE), .sel(OP[4:0]), .en(decoder_2_out1));  // open: out0, out2, out4, out5, out6, out7, out8, out9, out10, out12, out13, out14, out15, out16, out17, out18, out19, out20, out21, out22, out23, out24, out25, out26, out27, out28, out29, out30, out31
  or or_1 (PCAddSrc, BrIns[5], BrIns[4], ALUYSrc2);
  nor nor_1 (RFDinSrc[1], lw, BrIns[1]);
  or or_2 (RFDinSrc[0], lw, lh);
  and and_1 (Halt, syscall, v0_10);
  and and_2 (Disp, syscall, ~v0_10);  // AND_Gate
  Subtractor #(.width(32)) subtractor_1 (.a(v0), .b(32'ha), .out(subtractor_1_out));  // open: bin, bout
  or or_3 (RFR1Src, sll, sra, srl, sllv, srlv);
  or or_4 (ALUYSrc[1], addi, addiu, andi, ori, lw, DMWE, slti, lh);
  or or_5 (ALUYSrc[0], andi, sll, sra, srl, ori);
  or or_6 (ALUOP[3], \or , ori, \nor , slt, slti, sltu, ALUYSrc2);
  assign or_7_out = subtractor_1_out[7:0] | subtractor_1_out[15:8] | subtractor_1_out[23:16] | subtractor_1_out[31:24];  // OR_Gate or_7, 8 bits wide
  nor nor_2 (RFWE, DMWE, BrIns[5], BrIns[4], BrIns[2], BrIns[0], syscall, ALUYSrc2);
  or or_8 (ALUOP[1], \and , andi, srl, sub, \nor , BrIns[5], BrIns[4], slt, slti, srlv, ALUYSrc2);
  or or_9 (RFRWSrc[0], add, addu, \and , sll, sra, srl, sub, \or , \nor , slt, sltu, sllv, srlv);
  or or_10 (ALUOP[2], add, addi, addiu, addu, \and , andi, sub, lw, DMWE, BrIns[5], BrIns[4], sltu, lh);
  or or_11 (ALUOP[0], add, addi, addiu, addu, \and , andi, sra, lw, DMWE, slt, slti, lh, ALUYSrc2);
  nor nor_3 (v0_10, or_7_out[0], or_7_out[1], or_7_out[2], or_7_out[3], or_7_out[4], or_7_out[5], or_7_out[6], or_7_out[7]);
  Decoder #(.disabled(0)) decoder_4 (.out0(decoder_4_out0), .out1(decoder_4_out1), .sel(funct[5]), .en(decoder_1_out0));
  Decoder #(.select(5), .disabled(0)) decoder_5 (
    .out0(sll), .out2(srl), .out3(sra), .out4(sllv), .out6(srlv), .out8(BrIns[0]), .out12(syscall),
    .sel(funct[4:0]), .en(decoder_4_out0));  // open: out1, out5, out7, out9, out10, out11, out13, out14, out15, out16, out17, out18, out19, out20, out21, out22, out23, out24, out25, out26, out27, out28, out29, out30, out31
  Decoder #(.select(5), .disabled(0)) decoder_6 (
    .out0(add), .out1(addu), .out2(sub), .out4(\and ), .out5(\or ), .out7(\nor ), .out10(slt), .out11(sltu),
    .sel(funct[4:0]), .en(decoder_4_out1));  // open: out3, out6, out8, out9, out12, out13, out14, out15, out16, out17, out18, out19, out20, out21, out22, out23, out24, out25, out26, out27, out28, out29, out30, out31

  assign BrIns[3] = ALUYSrc2;
  assign PCEn = 1'b1;
  assign RFRWSrc[1] = BrIns[1];

  // Other names for the same wires on the sheet: jr = BrIns[0]; jal = BrIns[1]; j = BrIns[2]; bgez = ALUYSrc2;
  //   bne = BrIns[4]; beq = BrIns[5]; sw = DMWE
endmodule

module Branch (
  input  Equal,
  input  Judge,
  input  [5:0] BrIns,
  output [1:0] BrPCSrc,
  output PCSrc
);

  wire and_1_out, and_2_out, and_3_out, and_4_out, and_5_out, and_6_out, not_1_out, not_2_out, not_3_out;

  not not_1 (not_1_out, Judge);
  not not_2 (not_2_out, Equal);
  and and_1 (and_1_out, BrIns[5], Equal);
  and and_2 (and_2_out, BrIns[4], not_3_out);
  not not_3 (not_3_out, Equal);
  and and_3 (and_3_out, BrIns[5], Equal);
  and and_4 (and_4_out, BrIns[4], not_2_out);
  and and_5 (and_5_out, BrIns[3], not_1_out);
  and and_6 (and_6_out, BrIns[3], not_1_out);
  or or_1 (BrPCSrc[1], and_3_out, and_4_out, BrIns[2], BrIns[1], and_5_out);
  nor nor_1 (BrPCSrc[0], and_6_out, and_1_out, and_2_out, BrIns[0]);
  or or_2 (PCSrc, BrIns[5], BrIns[4], BrIns[3], BrIns[2], BrIns[1], BrIns[0]);

  // Other names for the same wires on the sheet: jr = BrIns[0]; jal = BrIns[1]; j = BrIns[2]; bgez = BrIns[3];
  //   bne = BrIns[4]; beq = BrIns[5]
endmodule

module IF_ID (
  input  [31:0] PC_1Din,
  input  [31:0] PCDin,
  input  [31:0] IRDin,
  input  WE,
  input  Clk,
  input  Rst,
  output [31:0] PC_1Dout,
  output [31:0] PCDout,
  output [31:0] IRDout
);

  Register #(.width(32)) PC_1 (.D(PC_1Din), .en(WE), .Q(PC_1Dout), .clk(Clk), .clr(Rst));
  Register #(.width(32)) PC (.D(PCDin), .en(WE), .Q(PCDout), .clk(Clk), .clr(Rst));
  Register #(.width(32)) IR (.D(IRDin), .en(WE), .Q(IRDout), .clk(Clk), .clr(Rst));
endmodule

module ID_EX (
  input  HaltDin,
  input  DispDin,
  input  [31:0] PC_1Din,
  input  [31:0] PCDin,
  input  [31:0] IRDin,
  input  [3:0] ALUOPDin,
  input  [1:0] ALUYSrcDin,
  input  ALUYSrc2Din,
  input  [31:0] RFR1Din,
  input  [31:0] RFR2Din,
  input  [31:0] Ext5to32Din,
  input  [31:0] SExt16to32Din,
  input  [31:0] Ext16to32Din,
  input  [31:0] SExt26to32Din,
  input  DMWEDin,
  input  PCAddSrcDin,
  input  RFWEDin,
  input  [1:0] RFDinSrcDin,
  input  [5:0] BrInsDin,
  input  [4:0] WRegDin,
  input  WE,
  input  Clk,
  input  Rst,
  output HaltDout,
  output DispDout,
  output [31:0] PC_1Dout,
  output [31:0] PCDout,
  output [31:0] IRDout,
  output [3:0] ALUOPDout,
  output [1:0] ALUYSrcDout,
  output ALUYSrc2Dout,
  output [31:0] RFR1Dout,
  output [31:0] RFR2Dout,
  output [31:0] Ext5to32Dout,
  output [31:0] SExt16to32Dout,
  output [31:0] Ext16to32Dout,
  output [31:0] SExt26to32Dout,
  output DMWEDout,
  output PCAddSrcDout,
  output RFWEDout,
  output [1:0] RFDinSrcDout,
  output [5:0] BrInsDout,
  output [4:0] WRegDout
);

  Register #(.width(1)) Halt (.D(HaltDin), .en(WE), .Q(HaltDout), .clk(Clk), .clr(Rst));
  Register #(.width(1)) Disp (.D(DispDin), .en(WE), .Q(DispDout), .clk(Clk), .clr(Rst));
  Register #(.width(32)) PC_1 (.D(PC_1Din), .en(WE), .Q(PC_1Dout), .clk(Clk), .clr(Rst));
  Register #(.width(32)) PC (.D(PCDin), .en(WE), .Q(PCDout), .clk(Clk), .clr(Rst));
  Register #(.width(32)) IR (.D(IRDin), .en(WE), .Q(IRDout), .clk(Clk), .clr(Rst));
  Register #(.width(4)) ALUOP (.D(ALUOPDin), .en(WE), .Q(ALUOPDout), .clk(Clk), .clr(Rst));
  Register #(.width(2)) ALUYSrc (.D(ALUYSrcDin), .en(WE), .Q(ALUYSrcDout), .clk(Clk), .clr(Rst));
  Register #(.width(1)) ALUYSrc2 (.D(ALUYSrc2Din), .en(WE), .Q(ALUYSrc2Dout), .clk(Clk), .clr(Rst));
  Register #(.width(32)) RFR1 (.D(RFR1Din), .en(WE), .Q(RFR1Dout), .clk(Clk), .clr(Rst));
  Register #(.width(32)) RFR2 (.D(RFR2Din), .en(WE), .Q(RFR2Dout), .clk(Clk), .clr(Rst));
  Register #(.width(32)) Ext5to32 (.D(Ext5to32Din), .en(WE), .Q(Ext5to32Dout), .clk(Clk), .clr(Rst));
  Register #(.width(32)) SExt16to32 (.D(SExt16to32Din), .en(WE), .Q(SExt16to32Dout), .clk(Clk), .clr(Rst));
  Register #(.width(32)) Ext16to32 (.D(Ext16to32Din), .en(WE), .Q(Ext16to32Dout), .clk(Clk), .clr(Rst));
  Register #(.width(32)) SExt26to32 (.D(SExt26to32Din), .en(WE), .Q(SExt26to32Dout), .clk(Clk), .clr(Rst));
  Register #(.width(1)) DMWE (.D(DMWEDin), .en(WE), .Q(DMWEDout), .clk(Clk), .clr(Rst));
  Register #(.width(1)) PCAddSrc (.D(PCAddSrcDin), .en(WE), .Q(PCAddSrcDout), .clk(Clk), .clr(Rst));
  Register #(.width(1)) RFWE (.D(RFWEDin), .en(WE), .Q(RFWEDout), .clk(Clk), .clr(Rst));
  Register #(.width(2)) RFDinSrc (.D(RFDinSrcDin), .en(WE), .Q(RFDinSrcDout), .clk(Clk), .clr(Rst));
  Register #(.width(6)) BrIns (.D(BrInsDin), .en(WE), .Q(BrInsDout), .clk(Clk), .clr(Rst));
  Register #(.width(5)) WReg (.D(WRegDin), .en(WE), .Q(WRegDout), .clk(Clk), .clr(Rst));
endmodule

module EX_MEM (
  input  DispDin,
  input  HaltDin,
  input  [31:0] PCDin,
  input  [31:0] IRDin,
  input  DMWEDin,
  input  RFWEDin,
  input  [1:0] RFDinSrcDin,
  input  [31:0] ALUDin,
  input  [31:0] RFR2Din,
  input  [31:0] PCAddDin,
  input  [4:0] WRegDin,
  input  WE,
  input  Clk,
  input  Rst,
  output DispDout,
  output HaltDout,
  output [31:0] PCDout,
  output [31:0] IRDout,
  output DMWEDout,
  output RFWEDout,
  output [1:0] RFDinSrcDout,
  output [31:0] ALUDout,
  output [31:0] RFR2Dout,
  output [31:0] PCAddDout,
  output [4:0] WRegDout
);

  Register #(.width(1)) Disp (.D(DispDin), .en(WE), .Q(DispDout), .clk(Clk), .clr(Rst));
  Register #(.width(1)) Halt (.D(HaltDin), .en(WE), .Q(HaltDout), .clk(Clk), .clr(Rst));
  Register #(.width(32)) PC (.D(PCDin), .en(WE), .Q(PCDout), .clk(Clk), .clr(Rst));
  Register #(.width(32)) IR (.D(IRDin), .en(WE), .Q(IRDout), .clk(Clk), .clr(Rst));
  Register #(.width(1)) DMWE (.D(DMWEDin), .en(WE), .Q(DMWEDout), .clk(Clk), .clr(Rst));
  Register #(.width(1)) RFWE (.D(RFWEDin), .en(WE), .Q(RFWEDout), .clk(Clk), .clr(Rst));
  Register #(.width(2)) RFDinSrc (.D(RFDinSrcDin), .en(WE), .Q(RFDinSrcDout), .clk(Clk), .clr(Rst));
  Register #(.width(32)) ALU (.D(ALUDin), .en(WE), .Q(ALUDout), .clk(Clk), .clr(Rst));
  Register #(.width(32)) RFR2 (.D(RFR2Din), .en(WE), .Q(RFR2Dout), .clk(Clk), .clr(Rst));
  Register #(.width(32)) PCAdd (.D(PCAddDin), .en(WE), .Q(PCAddDout), .clk(Clk), .clr(Rst));
  Register #(.width(5)) WReg (.D(WRegDin), .en(WE), .Q(WRegDout), .clk(Clk), .clr(Rst));
endmodule

module MEM_WB (
  input  DispDin,
  input  HaltDin,
  input  [31:0] PCDin,
  input  [31:0] IRDin,
  input  RFWEDin,
  input  [1:0] RFDinSrcDin,
  input  [31:0] ALUDin,
  input  [31:0] DMDin,
  input  [31:0] SExt16to32Din,
  input  [31:0] PCAddDin,
  input  [4:0] WRegDin,
  input  WE,
  input  Clk,
  input  Rst,
  output DispDout,
  output HaltDout,
  output [31:0] PCDout,
  output [31:0] IRDout,
  output RFWEDout,
  output [1:0] RFDinSrcDout,
  output [31:0] ALUDout,
  output [31:0] DMDout,
  output [31:0] SExt16to32Dout,
  output [31:0] PCAddDout,
  output [4:0] WRegDout
);

  Register #(.width(1)) Disp (.D(DispDin), .en(WE), .Q(DispDout), .clk(Clk), .clr(Rst));
  Register #(.width(1)) Halt (.D(HaltDin), .en(WE), .Q(HaltDout), .clk(Clk), .clr(Rst));
  Register #(.width(32)) PC (.D(PCDin), .en(WE), .Q(PCDout), .clk(Clk), .clr(Rst));
  Register #(.width(32)) IR (.D(IRDin), .en(WE), .Q(IRDout), .clk(Clk), .clr(Rst));
  Register #(.width(1)) RFWE (.D(RFWEDin), .en(WE), .Q(RFWEDout), .clk(Clk), .clr(Rst));
  Register #(.width(2)) RFDinSrc (.D(RFDinSrcDin), .en(WE), .Q(RFDinSrcDout), .clk(Clk), .clr(Rst));
  Register #(.width(32)) ALU (.D(ALUDin), .en(WE), .Q(ALUDout), .clk(Clk), .clr(Rst));
  Register #(.width(32)) DM (.D(DMDin), .en(WE), .Q(DMDout), .clk(Clk), .clr(Rst));
  Register #(.width(32)) SExt16to32 (.D(SExt16to32Din), .en(WE), .Q(SExt16to32Dout), .clk(Clk), .clr(Rst));
  Register #(.width(32)) PCAdd (.D(PCAddDin), .en(WE), .Q(PCAddDout), .clk(Clk), .clr(Rst));
  Register #(.width(5)) WReg (.D(WRegDin), .en(WE), .Q(WRegDout), .clk(Clk), .clr(Rst));
endmodule
