// Logisim project ext-cpu.circ as structural Verilog
module main (
);

  wire alu_1_equal, Clk, ComClk, control_1_aluysrc2, control_1_disp, control_1_dmwe, control_1_halt,
       control_1_pcaddsrc, control_1_pcen, control_1_rfr1src, control_1_rfwe, not_1_out;
  wire [1:0] control_1_aluysrc, control_1_pcsrc, control_1_rfdinsrc, control_1_rfrwsrc;
  wire [3:0] control_1_aluop, Disp_q, Disp_q_2, Disp_q_3, Disp_q_4, Disp_q_5, Disp_q_6, Disp_q_7, Disp_q_8;
  wire [4:0] insanalyse_1_rd, insanalyse_1_rs, insanalyse_1_rt, insanalyse_1_shamt, multiplexer_2_out,
       multiplexer_3_out, multiplexer_4_out;
  wire [5:0] insanalyse_1_funct, insanalyse_1_op;
  wire [15:0] insanalyse_1_immediate16, ram_1_data;
  wire [25:0] insanalyse_1_immediate26;
  wire [31:0] adder_1_out, adder_2_out, alu_1_result, bit_extender_1_out, bit_extender_2_out,
       bit_extender_3_out, bit_extender_4_out, bit_extender_5_out, counter_1_q, main_1_a0_value, main_1_reg1,
       main_1_reg2_2, main_1_v0_value, multiplexer_1_out, multiplexer_5_out, multiplexer_6_out,
       multiplexer_7_out, multiplexer_8_out, PC_q, rom_1_data;
  wire [31:16] ram_1_data_2;

  assign bit_extender_1_out = {{6{1'b0}}, insanalyse_1_immediate26};  // Bit_Extender bit_extender_1
  Multiplexer #(.select(2), .width(32), .enable("false")) multiplexer_1 (
    .in0(main_1_reg1), .in1(adder_1_out), .in2(adder_2_out), .in3(bit_extender_1_out),
    .out(multiplexer_1_out), .sel(control_1_pcsrc));
  Register #(.width(32)) PC (.D(multiplexer_1_out), .en(control_1_pcen), .Q(PC_q), .clk(Clk), .clr(1'b0));
  Adder #(.width(32)) adder_1 (.a(32'h1), .b(PC_q), .out(adder_1_out), .cin(1'b0));  // open: cout
  Hex_Digit_Display hex_digit_display_1 (.value(Disp_q_8), .dp(1'b0));
  Hex_Digit_Display hex_digit_display_2 (.value(Disp_q_7), .dp(1'b0));
  Hex_Digit_Display hex_digit_display_3 (.value(Disp_q_5), .dp(1'b0));
  Hex_Digit_Display hex_digit_display_4 (.value(Disp_q_6), .dp(1'b0));
  Hex_Digit_Display hex_digit_display_5 (.value(Disp_q_4), .dp(1'b0));
  Hex_Digit_Display hex_digit_display_6 (.value(Disp_q_3), .dp(1'b0));
  Hex_Digit_Display hex_digit_display_7 (.value(Disp_q_2), .dp(1'b0));
  Hex_Digit_Display hex_digit_display_8 (.value(Disp_q), .dp(1'b0));
  ROM #(.addrWidth(10), .dataWidth(32)) rom_1 (.addr(PC_q[9:0]), .data(rom_1_data), .sel(1'b1));
  Counter #(.width(32), .max('hffffffff)) counter_1 (.Q(counter_1_q), .clk(Clk));  // open: load, D, count, carry, clr
  // Probe on counter_1_q
  Clock clock_1 (.out(ComClk));
  and and_1 (Clk, ComClk, ~control_1_halt);  // AND_Gate
  Register #(.width(32), .trigger("high")) Disp (
    .D(main_1_a0_value), .en(1'b1),
    .Q({Disp_q_8, Disp_q_7, Disp_q_6, Disp_q_5, Disp_q_4, Disp_q_3, Disp_q_2, Disp_q}), .clk(control_1_disp),
    .clr(1'b0));
  InsAnalyse insanalyse_1 (
    .Ins(rom_1_data), .OP(insanalyse_1_op), .Rs(insanalyse_1_rs), .Rt(insanalyse_1_rt), .Rd(insanalyse_1_rd),
    .Shamt(insanalyse_1_shamt), .funct(insanalyse_1_funct), .Immediate16(insanalyse_1_immediate16),
    .Immediate26(insanalyse_1_immediate26));
  Control control_1 (
    .Equal(alu_1_equal), .v0(main_1_v0_value), .OP(insanalyse_1_op), .funct(insanalyse_1_funct),
    .PCSrc(control_1_pcsrc), .PCAddSrc(control_1_pcaddsrc), .PCEn(control_1_pcen),
    .RFR1Src(control_1_rfr1src), .RFRWSrc(control_1_rfrwsrc), .RFDinSrc(control_1_rfdinsrc),
    .RFWE(control_1_rfwe), .ALUYSrc(control_1_aluysrc), .ALUOP(control_1_aluop), .DMWE(control_1_dmwe),
    .Halt(control_1_halt), .Disp(control_1_disp), .Judge(alu_1_result[0]), .ALUYSrc2(control_1_aluysrc2));
  not not_1 (not_1_out, control_1_rfr1src);
  Multiplexer #(.width(5), .enable("false")) multiplexer_2 (
    .in0(insanalyse_1_rs), .in1(insanalyse_1_rt), .out(multiplexer_2_out), .sel(control_1_rfr1src));
  Multiplexer #(.width(5), .enable("false")) multiplexer_3 (
    .in0(insanalyse_1_rs), .in1(insanalyse_1_rt), .out(multiplexer_3_out), .sel(not_1_out));
  Multiplexer #(.select(2), .width(5), .enable("false")) multiplexer_4 (
    .in0(insanalyse_1_rt), .in1(insanalyse_1_rd), .in2({5{1'b1}}), .out(multiplexer_4_out),
    .sel(control_1_rfrwsrc));  // open: in3
  Multiplexer #(.select(2), .width(32), .enable("false")) multiplexer_5 (
    .in0(adder_2_out), .in1({ram_1_data_2, ram_1_data}), .in2(alu_1_result), .in3(bit_extender_5_out),
    .out(multiplexer_5_out), .sel(control_1_rfdinsrc));
  regfile_cpu_main main_1 (
    .Reg1_num(multiplexer_2_out), .Reg2(multiplexer_3_out), .Write_Reg_num(multiplexer_4_out),
    .Din(multiplexer_5_out), .Write_Enable(control_1_rfwe), .Clock(Clk), .Reg1(main_1_reg1),
    .Reg2_2(main_1_reg2_2), .v0_Value(main_1_v0_value), .a0_Value(main_1_a0_value));  // open: s0_Value, s1_Value, s2_Value, ra_Value
  assign bit_extender_2_out = {{27{1'b0}}, insanalyse_1_shamt};  // Bit_Extender bit_extender_2
  assign bit_extender_3_out = {{16{insanalyse_1_immediate16[15]}}, insanalyse_1_immediate16};  // Bit_Extender bit_extender_3
  assign bit_extender_4_out = {{16{1'b0}}, insanalyse_1_immediate16};  // Bit_Extender bit_extender_4
  Multiplexer #(.select(2), .width(32), .enable("false")) multiplexer_6 (
    .in0(main_1_reg2_2), .in1(bit_extender_2_out), .in2(bit_extender_3_out), .in3(bit_extender_4_out),
    .out(multiplexer_6_out), .sel(control_1_aluysrc));
  ALU alu_1 (
    .AluOP(control_1_aluop), .X(main_1_reg1), .Equal(alu_1_equal), .Result(alu_1_result),
    .Y(multiplexer_7_out));  // open: Signed_Overflow, Result_2, UnSigned_Overflow
  Multiplexer #(.width(32), .disabled(0), .enable("false")) multiplexer_7 (
    .in0(multiplexer_6_out), .in1({32{1'b0}}), .out(multiplexer_7_out), .sel(control_1_aluysrc2));
  Multiplexer #(.width(32), .enable("false")) multiplexer_8 (
    .in0({32{1'b0}}), .in1(bit_extender_3_out), .out(multiplexer_8_out), .sel(control_1_pcaddsrc));
  RAM #(.addrWidth(10), .dataWidth(32), .bus("separate")) ram_1 (
    .addr(alu_1_result[9:0]), .din(main_1_reg2_2), .data({ram_1_data_2, ram_1_data}), .str(control_1_dmwe),
    .sel(1'b1), .clk(ComClk), .ld(1'b1), .clr(1'b0));
  assign bit_extender_5_out = {{16{ram_1_data[15]}}, ram_1_data};  // Bit_Extender bit_extender_5
  Adder #(.width(32)) adder_2 (.a(adder_1_out), .b(multiplexer_8_out), .out(adder_2_out), .cin(1'b0));  // open: cout

  // Notes on the sheet:
  //   contents of rom_1 (hex, n*v repeats v):
  //   20040008 20080008 20100004 20110006 20020001 c 2042004 882020 c 2231ffff 621fffb 49020 ac440000
  //   84440000 c 122020 20110007 2042006 c 2231ffff 621fffc 2002000a c
endmodule

module InsAnalyse (
  input  [31:0] Ins,
  output [5:0] OP,
  output [4:0] Rs,
  output [4:0] Rt,
  output [4:0] Rd,
  output [4:0] Shamt,
  output [5:0] funct,
  output [15:0] Immediate16,
  output [25:0] Immediate26
);


  assign funct = Ins[5:0];
  assign Immediate16 = Ins[15:0];
  assign Immediate26 = Ins[25:0];
  assign OP = Ins[31:26];
  assign Rd = Ins[15:11];
  assign Rs = Ins[25:21];
  assign Rt = Ins[20:16];
  assign Shamt = Ins[10:6];
endmodule

module Control (
  input  Equal,
  input  Judge,
  input  [31:0] v0,
  input  [5:0] OP,
  input  [5:0] funct,
  output [1:0] PCSrc,
  output PCAddSrc,
  output PCEn,
  output RFR1Src,
  output [1:0] RFRWSrc,
  output [1:0] RFDinSrc,
  output RFWE,
  output [1:0] ALUYSrc,
  output ALUYSrc2,
  output [3:0] ALUOP,
  output DMWE,
  output Halt,
  output Disp
);

  wire add, addi, addiu, addu, \and , and_3_out, and_4_out, and_5_out, and_6_out, and_7_out, and_8_out, andi,
       beq, bne, decoder_1_out0, decoder_2_out0, decoder_2_out1, decoder_4_out0, decoder_4_out1, j, jr, lh,
       lw, \nor , not_1_out, not_2_out, not_3_out, \or , ori, sll, sllv, slt, slti, sltu, sra, srl, srlv,
       sub, syscall, v0_10;
  wire [7:0] or_7_out;
  wire [31:0] subtractor_1_out;

  Decoder #(.select(5), .disabled(0)) decoder_1 (
    .out0(decoder_1_out0), .out1(ALUYSrc2), .out2(j), .out3(RFRWSrc[1]), .out4(beq), .out5(bne), .out8(addi),
    .out9(addiu), .out10(slti), .out12(andi), .out13(ori), .sel(OP[4:0]), .en(decoder_2_out0));  // open: out6, out7, out11, out14, out15, out16, out17, out18, out19, out20, out21, out22, out23, out24, out25, out26, out27, out28, out29, out30, out31
  Decoder #(.enable("false")) decoder_2 (.out0(decoder_2_out0), .out1(decoder_2_out1), .sel(OP[5]));
  Decoder #(.select(5), .disabled(0)) decoder_3 (
    .out1(lh), .out3(lw), .out11(DMWE), .sel(OP[4:0]), .en(decoder_2_out1));  // open: out0, out2, out4, out5, out6, out7, out8, out9, out10, out12, out13, out14, out15, out16, out17, out18, out19, out20, out21, out22, out23, out24, out25, out26, out27, out28, out29, out30, out31
  not not_1 (not_1_out, Judge);
  or or_1 (PCAddSrc, beq, bne, ALUYSrc2);
  nor nor_1 (RFDinSrc[1], lw, RFRWSrc[1]);
  or or_2 (RFDinSrc[0], lw, lh);
  and and_1 (Halt, syscall, v0_10);
  and and_2 (Disp, syscall, ~v0_10);  // AND_Gate
  Subtractor #(.width(32)) subtractor_1 (.a(v0), .b(32'ha), .out(subtractor_1_out));  // open: bin, bout
  not not_2 (not_2_out, Equal);
  and and_3 (and_3_out, beq, Equal);
  and and_4 (and_4_out, bne, not_3_out);
  not not_3 (not_3_out, Equal);
  or or_3 (RFR1Src, sll, sra, srl, sllv, srlv);
  or or_4 (ALUYSrc[1], addi, addiu, andi, ori, lw, DMWE, slti, lh);
  or or_5 (ALUYSrc[0], andi, sll, sra, srl, ori);
  or or_6 (ALUOP[3], \or , ori, \nor , slt, slti, sltu, ALUYSrc2);
  assign or_7_out = subtractor_1_out[7:0] | subtractor_1_out[15:8] | subtractor_1_out[23:16] | subtractor_1_out[31:24];  // OR_Gate or_7, 8 bits wide
  and and_5 (and_5_out, beq, Equal);
  and and_6 (and_6_out, bne, not_2_out);
  and and_7 (and_7_out, ALUYSrc2, not_1_out);
  and and_8 (and_8_out, ALUYSrc2, not_1_out);
  nor nor_2 (RFWE, DMWE, beq, bne, j, jr, syscall, ALUYSrc2);
  or or_8 (ALUOP[1], \and , andi, srl, sub, \nor , beq, bne, slt, slti, srlv, ALUYSrc2);
  or or_9 (PCSrc[1], and_5_out, and_6_out, j, RFRWSrc[1], and_7_out);
  nor nor_3 (PCSrc[0], and_8_out, and_3_out, and_4_out, jr);
  or or_10 (RFRWSrc[0], add, addu, \and , sll, sra, srl, sub, \or , \nor , slt, sltu, sllv, srlv);
  or or_11 (ALUOP[2], add, addi, addiu, addu, \and , andi, sub, lw, DMWE, beq, bne, sltu, lh);
  or or_12 (ALUOP[0], add, addi, addiu, addu, \and , andi, sra, lw, DMWE, slt, slti, lh, ALUYSrc2);
  nor nor_4 (v0_10, or_7_out[0], or_7_out[1], or_7_out[2], or_7_out[3], or_7_out[4], or_7_out[5], or_7_out[6], or_7_out[7]);
  Decoder #(.disabled(0)) decoder_4 (.out0(decoder_4_out0), .out1(decoder_4_out1), .sel(funct[5]), .en(decoder_1_out0));
  Decoder #(.select(5), .disabled(0)) decoder_5 (
    .out0(sll), .out2(srl), .out3(sra), .out4(sllv), .out6(srlv), .out8(jr), .out12(syscall),
    .sel(funct[4:0]), .en(decoder_4_out0));  // open: out1, out5, out7, out9, out10, out11, out13, out14, out15, out16, out17, out18, out19, out20, out21, out22, out23, out24, out25, out26, out27, out28, out29, out30, out31
  Decoder #(.select(5), .disabled(0)) decoder_6 (
    .out0(add), .out1(addu), .out2(sub), .out4(\and ), .out5(\or ), .out7(\nor ), .out10(slt), .out11(sltu),
    .sel(funct[4:0]), .en(decoder_4_out1));  // open: out3, out6, out8, out9, out12, out13, out14, out15, out16, out17, out18, out19, out20, out21, out22, out23, out24, out25, out26, out27, out28, out29, out30, out31

  assign PCEn = 1'b1;

  // Other names for the same wires on the sheet: bgez = ALUYSrc2; jal = RFRWSrc[1]; sw = DMWE
endmodule

module IR (
  input  Rst,
  input  IE,
  input  IEW,
  input  INMW,
  input  [3:0] INM,
  input  IR0,
  input  IR1,
  input  IR2,
  input  IR3,
  output [1:0] IRNUM,
  output IR
);

  wire and_1_out, and_2_out, and_3_out, and_4_out, Clk, not_1_out, not_2_out, not_3_out, not_4_out,
       priority_encoder_1_gs, register_1_q, register_2_q, register_3_q, register_4_q, register_5_q,
       register_6_q, register_7_q, register_8_q, register_9_q;

  Clock u_Clk (.out(Clk));
  Register #(.width(1)) register_1 (.D(1'b1), .en(1'b1), .Q(register_1_q), .clk(IR0), .clr(Rst));
  Register #(.width(1)) register_2 (.D(1'b1), .en(1'b1), .Q(register_2_q), .clk(IR1), .clr(Rst));
  Register #(.width(1)) register_3 (.D(1'b1), .en(1'b1), .Q(register_3_q), .clk(IR2), .clr(Rst));
  Register #(.width(1)) register_4 (.D(1'b1), .en(1'b1), .Q(register_4_q), .clk(IR3), .clr(Rst));
  Register #(.width(1)) register_5 (.D(INM[0]), .en(INMW), .Q(register_5_q), .clk(Clk), .clr(Rst));
  not not_1 (not_1_out, register_5_q);
  Register #(.width(1)) register_6 (.D(INM[1]), .en(INMW), .Q(register_6_q), .clk(Clk), .clr(Rst));
  not not_2 (not_2_out, register_6_q);
  not not_3 (not_3_out, register_7_q);
  Register #(.width(1)) register_7 (.D(INM[2]), .en(INMW), .Q(register_7_q), .clk(Clk), .clr(Rst));
  Register #(.width(1)) register_8 (.D(INM[3]), .en(INMW), .Q(register_8_q), .clk(Clk), .clr(Rst));
  not not_4 (not_4_out, register_8_q);
  and and_1 (and_1_out, register_1_q, not_1_out);
  and and_2 (and_2_out, register_2_q, not_2_out);
  and and_3 (and_3_out, register_3_q, not_3_out);
  and and_4 (and_4_out, register_4_q, not_4_out);
  Priority_Encoder #(.select(2), .disabled(0)) priority_encoder_1 (
    .in0(and_1_out), .in1(and_2_out), .in2(and_3_out), .in3(and_4_out), .out(IRNUM),
    .gs(priority_encoder_1_gs), .en_in(1'b1));  // open: en_out
  Register #(.width(1)) register_9 (.D(IE), .en(IEW), .Q(register_9_q), .clk(Clk), .clr(Rst));
  and and_5 (IR, priority_encoder_1_gs, register_9_q);
endmodule
